// Logisim project 4_bit_register_circ.circ as structural Verilog: 1 circuit, main circuit main
module main (
);

  wire d_ff_1_q, undriven, undriven_2, undriven_3;

  D_Flip_Flop d_ff_1 (.D(undriven), .clk(undriven_3), .Q(d_ff_1_q), .preset(undriven_2));  // open: Qn, reset
  D_Flip_Flop d_ff_2 (.D(undriven), .clk(undriven_3), .Q(d_ff_1_q), .preset(undriven_2));  // open: Qn, reset
  D_Flip_Flop d_ff_3 (.D(undriven), .clk(undriven_3), .Q(d_ff_1_q), .preset(undriven_2));  // open: Qn, reset
  D_Flip_Flop d_ff_4 (.D(undriven), .clk(undriven_3), .Q(d_ff_1_q), .preset(undriven_2));  // open: Qn, reset
endmodule
