// Logisim project adder_circ.circ as structural Verilog: 1 circuit, main circuit main
module main (
);

  wire and_1_out, and_2_out, and_3_out, and_4_out, and_5_out, and_6_out, and_7_out, and_8_out, or_1_out,
       or_2_out, or_3_out, or_4_out, undriven, undriven_2, undriven_3, xor_1_out, xor_2_out, xor_3_out,
       xor_4_out, xor_5_out, xor_6_out, xor_7_out, xor_8_out;

  xor xor_1 (xor_1_out, undriven_2, undriven_3);
  and and_1 (and_1_out, undriven_2, undriven_3);
  xor xor_2 (xor_2_out, or_1_out, or_1_out);
  and and_2 (and_2_out, or_1_out, or_1_out);
  xor xor_3 (xor_3_out, or_2_out, or_2_out);
  and and_3 (and_3_out, or_2_out, or_2_out);
  xor xor_4 (xor_4_out, or_3_out, or_3_out);
  and and_4 (and_4_out, or_3_out, or_3_out);
  and and_5 (and_5_out, undriven, xor_1_out);
  and and_6 (and_6_out, or_1_out, xor_2_out);
  and and_7 (and_7_out, or_2_out, xor_3_out);
  xor xor_5 (xor_5_out, undriven, xor_1_out);
  xor xor_6 (xor_6_out, or_1_out, xor_2_out);
  xor xor_7 (xor_7_out, or_2_out, xor_3_out);
  xor xor_8 (xor_8_out, or_3_out, xor_4_out);
  and and_8 (and_8_out, or_3_out, xor_4_out);
  or or_1 (or_1_out, and_5_out, and_1_out);
  or or_2 (or_2_out, and_6_out, and_2_out);
  or or_3 (or_3_out, and_7_out, and_3_out);
  or or_4 (or_4_out, and_8_out, and_4_out);
endmodule
