// Logisim project alu.circ as structural Verilog: 2 circuits, main circuit main
module main (
);

  wire adder_1_out, and_1_out, multiplexer_1_out, or_1_out, subtractor_1_out, undriven, undriven_2;
  wire [1:0] undriven_3;

  fourbitregister fourbitregister_1 ();
  fourbitregister fourbitregister_2 ();
  Adder #(.width(1)) adder_1 (.a(undriven), .b(undriven_2), .out(adder_1_out));  // open: cin, cout
  Subtractor #(.width(1)) subtractor_1 (.a(undriven), .b(undriven_2), .out(subtractor_1_out));  // open: bin, bout
  and and_1 (and_1_out, undriven_2, undriven);
  or or_1 (or_1_out, undriven_2, undriven);
  Multiplexer #(.disabled("Z"), .enable("true"), .select(2)) multiplexer_1 (
    .in0(adder_1_out), .in1(subtractor_1_out), .in2(and_1_out), .in3(or_1_out), .out(multiplexer_1_out),
    .sel(undriven_3));  // open: en
endmodule

module fourbitregister (
);

  wire d_ff_1_q, d_ff_2_q;

  D_Flip_Flop d_ff_1 (.D(d_ff_1_q), .clk(d_ff_1_q), .Q(d_ff_1_q), .preset(d_ff_1_q));  // open: Qn, reset
  D_Flip_Flop d_ff_2 (.D(d_ff_2_q), .clk(d_ff_2_q), .Q(d_ff_2_q), .preset(d_ff_2_q));  // open: Qn, reset
  D_Flip_Flop d_ff_3 (.D(d_ff_1_q), .clk(d_ff_1_q), .Q(d_ff_1_q), .preset(d_ff_1_q));  // open: Qn, reset
  D_Flip_Flop d_ff_4 (.D(d_ff_2_q), .clk(d_ff_2_q), .Q(d_ff_2_q), .preset(d_ff_2_q));  // open: Qn, reset
  D_Flip_Flop d_ff_5 (.D(d_ff_1_q), .clk(d_ff_1_q), .Q(d_ff_1_q), .preset(d_ff_1_q));  // open: Qn, reset
  D_Flip_Flop d_ff_6 (.D(d_ff_2_q), .clk(d_ff_2_q), .Q(d_ff_2_q), .preset(d_ff_2_q));  // open: Qn, reset
  D_Flip_Flop d_ff_7 (.D(d_ff_1_q), .clk(d_ff_1_q), .Q(d_ff_1_q), .preset(d_ff_1_q));  // open: Qn, reset
  D_Flip_Flop d_ff_8 (.D(d_ff_2_q), .clk(d_ff_2_q), .Q(d_ff_2_q), .preset(d_ff_2_q));  // open: Qn, reset
endmodule
