// Logisim project security_chip.circ as structural Verilog: 1 circuit, main circuit main
// detector
module main (
);

  wire and_1_out, or_1_out, or_2_out, undriven, undriven_2, undriven_3, undriven_4;

  or or_1 (or_1_out, undriven_2, undriven_3);
  or or_2 (or_2_out, or_1_out, undriven_4);
  and and_1 (and_1_out, undriven, or_2_out);

  // Notes on the sheet:
  //   Armed
  //   Door
  //   Glass
  //   Motion
endmodule
